// Logisim project 4.3.circ as structural Verilog: 7 circuits, main circuit main
module main (
  input  in_1,
  input  [19:0] in_2,
  input  in_3,
  input  [15:0] in_4,
  input  in_5,
  input  in_6,
  output [15:0] out_7
);

  wire and_1_out, cpu_1_a0, cpu_1_a1, cpu_1_a2, cpu_1_a3, cpu_1_a4, cpu_1_a5, cpu_1_a6, cpu_1_a7, cpu_1_a8,
       cpu_1_a9, cpu_1_a10, cpu_1_a11, cpu_1_a12, cpu_1_a13, cpu_1_a14, cpu_1_a15, cpu_1_a16, cpu_1_a17,
       cpu_1_a18, cpu_1_a19, cpu_1_bhe_out, cpu_1_out_8, cpu_1_out_32, cpu_1_out_33, n74138_1_pin9,
       n74138_1_pin10, n74138_1_pin11, n74138_1_pin13, n74138_1_pin14, n74138_1_pin15, nor_1_out, nor_2_out,
       nor_3_out, nor_4_out, not_1_out, not_2_out, not_3_out, not_4_out, not_5_out, not_6_out, not_7_out,
       not_8_out;
  wire [7:0] cpu_1_w, cpu_1_w_2;

  CPU cpu_1 (
    .IO_M(in_1), .RD(in_5), .WR(in_6), .address(in_2), .BHE(in_3), .Data_in(in_4), .R({cpu_1_w_2, cpu_1_w}),
    .Data_out(out_7), .out_8(cpu_1_out_8), .W({cpu_1_w_2, cpu_1_w}), .BHE_out(cpu_1_bhe_out),
    .out_32(cpu_1_out_32), .out_33(cpu_1_out_33), .A19(cpu_1_a19), .A18(cpu_1_a18), .A17(cpu_1_a17),
    .A16(cpu_1_a16), .A15(cpu_1_a15), .A14(cpu_1_a14), .A13(cpu_1_a13), .A12(cpu_1_a12), .A11(cpu_1_a11),
    .A10(cpu_1_a10), .A9(cpu_1_a9), .A8(cpu_1_a8), .A7(cpu_1_a7), .A6(cpu_1_a6), .A5(cpu_1_a5),
    .A4(cpu_1_a4), .A3(cpu_1_a3), .A2(cpu_1_a2), .A1(cpu_1_a1), .A0(cpu_1_a0));
  and and_1 (and_1_out, cpu_1_a19, cpu_1_a18, cpu_1_a17);
  _74138 #(.ShowInternalStructure("true")) u_74138_1 (
    .pin1(cpu_1_a0), .pin2(cpu_1_bhe_out), .pin3(cpu_1_a16), .pin4(cpu_1_out_8), .pin5(cpu_1_out_8),
    .pin6(and_1_out), .pin15(n74138_1_pin15), .pin14(n74138_1_pin14), .pin13(n74138_1_pin13),
    .pin11(n74138_1_pin11), .pin10(n74138_1_pin10), .pin9(n74138_1_pin9));  // open: pin7, pin12
  not not_1 (not_1_out, n74138_1_pin11);
  not not_2 (not_2_out, n74138_1_pin10);
  nor nor_1 (nor_1_out, not_1_out, not_2_out);
  My_ROM my_rom_1 (
    .A4(cpu_1_a5), .A3(cpu_1_a4), .A2(cpu_1_a3), .A1(cpu_1_a2), .A0(cpu_1_a1), .OE(cpu_1_out_32),
    .CE(nor_1_out), .A14(cpu_1_a15), .A13(cpu_1_a14), .A12(cpu_1_a13), .A11(cpu_1_a12), .A10(cpu_1_a11),
    .A9(cpu_1_a10), .A8(cpu_1_a9), .A7(cpu_1_a8), .A6(cpu_1_a7), .A5(cpu_1_a6), .data(cpu_1_w_2));
  not not_3 (not_3_out, n74138_1_pin11);
  not not_4 (not_4_out, n74138_1_pin9);
  nor nor_2 (nor_2_out, not_3_out, not_4_out);
  My_ROM my_rom_2 (
    .A4(cpu_1_a5), .A3(cpu_1_a4), .A2(cpu_1_a3), .A1(cpu_1_a2), .A0(cpu_1_a1), .OE(cpu_1_out_32),
    .CE(nor_2_out), .A14(cpu_1_a15), .A13(cpu_1_a14), .A12(cpu_1_a13), .A11(cpu_1_a12), .A10(cpu_1_a11),
    .A9(cpu_1_a10), .A8(cpu_1_a9), .A7(cpu_1_a8), .A6(cpu_1_a7), .A5(cpu_1_a6), .data(cpu_1_w));
  not not_5 (not_5_out, n74138_1_pin15);
  nor nor_3 (nor_3_out, not_5_out, not_6_out);
  not not_6 (not_6_out, n74138_1_pin13);
  My_RAM my_ram_1 (
    .A4(cpu_1_a5), .A3(cpu_1_a4), .A2(cpu_1_a3), .A1(cpu_1_a2), .A0(cpu_1_a1), .OE(cpu_1_out_32),
    .CE(nor_3_out), .WR(cpu_1_out_33), .A14(cpu_1_a15), .A13(cpu_1_a14), .A12(cpu_1_a13), .A11(cpu_1_a12),
    .A10(cpu_1_a11), .A9(cpu_1_a10), .A8(cpu_1_a9), .A7(cpu_1_a8), .A6(cpu_1_a7), .A5(cpu_1_a6),
    .data(cpu_1_w_2));
  not not_7 (not_7_out, n74138_1_pin14);
  not not_8 (not_8_out, n74138_1_pin13);
  nor nor_4 (nor_4_out, not_7_out, not_8_out);
  My_RAM my_ram_2 (
    .A4(cpu_1_a5), .A3(cpu_1_a4), .A2(cpu_1_a3), .A1(cpu_1_a2), .A0(cpu_1_a1), .OE(cpu_1_out_32),
    .CE(nor_4_out), .WR(cpu_1_out_33), .A14(cpu_1_a15), .A13(cpu_1_a14), .A12(cpu_1_a13), .A11(cpu_1_a12),
    .A10(cpu_1_a11), .A9(cpu_1_a10), .A8(cpu_1_a9), .A7(cpu_1_a8), .A6(cpu_1_a7), .A5(cpu_1_a6),
    .data(cpu_1_w));
endmodule

module CPU (
  input  IO_M,
  input  [19:0] address,
  input  BHE,
  input  [15:0] R,
  input  [15:0] Data_in,
  input  RD,
  input  WR,
  output out_8,
  output A19,
  output A18,
  output A17,
  output A16,
  output A15,
  output A14,
  output A13,
  output A12,
  output A11,
  output A10,
  output A9,
  output A8,
  output A7,
  output A6,
  output A5,
  output A4,
  output A3,
  output A2,
  output A1,
  output BHE_out,
  output A0,
  output [15:0] Data_out,
  output [15:0] W,
  output out_32,
  output out_33
);

  wire and_1_out, and_2_out, not_1_out, not_2_out;

  not not_1 (not_1_out, RD);
  and and_1 (and_1_out, not_1_out, RD);
  assign Data_in = and_1_out ? W : 16'bz;  // Controlled_Buffer controlled_buffer_1
  bit_20 bit_20_1 (
    .data(address), .A0(A0), .A1(A1), .A2(A2), .A3(A3), .A4(A4), .A5(A5), .A6(A6), .A7(A7), .A8(A8), .A9(A9),
    .A10(A10), .A11(A11), .A12(A12), .A13(A13), .A14(A14), .A15(A15), .A16(A16), .A17(A17), .A18(A18),
    .A19(A9));
  and and_2 (and_2_out, not_2_out, RD);
  assign Data_out = and_2_out ? R : 16'bz;  // Controlled_Buffer controlled_buffer_2
  not not_2 (not_2_out, WR);

  assign A19 = A9;
  assign BHE_out = BHE;
  assign out_8 = IO_M;
  assign out_32 = RD;
  assign out_33 = WR;
endmodule

module bit_16 (
  input  [15:0] data,
  output A0,
  output A1,
  output A2,
  output A3,
  output A4,
  output A5,
  output A6,
  output A7,
  output A8,
  output A9,
  output A10,
  output A11,
  output A12,
  output A13,
  output A14,
  output A15
);


  assign A0 = data[0];
  assign A1 = data[1];
  assign A2 = data[2];
  assign A3 = data[3];
  assign A4 = data[4];
  assign A5 = data[5];
  assign A6 = data[6];
  assign A7 = data[7];
  assign A8 = data[8];
  assign A9 = data[9];
  assign A10 = data[10];
  assign A11 = data[11];
  assign A12 = data[12];
  assign A13 = data[13];
  assign A14 = data[14];
  assign A15 = data[15];
endmodule

module bit_20 (
  input  [19:0] data,
  output A0,
  output A1,
  output A2,
  output A3,
  output A4,
  output A5,
  output A6,
  output A7,
  output A8,
  output A9,
  output A10,
  output A11,
  output A12,
  output A13,
  output A14,
  output A15,
  output A16,
  output A17,
  output A18,
  output A19
);


  assign A0 = data[0];
  assign A1 = data[1];
  assign A2 = data[2];
  assign A3 = data[3];
  assign A4 = data[4];
  assign A5 = data[5];
  assign A6 = data[6];
  assign A7 = data[7];
  assign A8 = data[8];
  assign A9 = data[9];
  assign A10 = data[10];
  assign A11 = data[11];
  assign A12 = data[12];
  assign A13 = data[13];
  assign A14 = data[14];
  assign A15 = data[15];
  assign A16 = data[16];
  assign A17 = data[17];
  assign A18 = data[18];
  assign A19 = data[19];
endmodule

module address (
  input  in_1,
  input  in_2,
  input  in_3,
  input  in_4,
  input  in_5,
  input  in_6,
  input  in_7,
  input  in_8,
  input  in_9,
  input  in_10,
  input  in_11,
  input  in_12,
  input  in_13,
  input  in_14,
  input  in_15,
  output [14:0] out_16
);


  assign out_16 = {in_15, in_14, in_13, in_12, in_11, in_10, in_9, in_8, in_7, in_6, in_5, in_4, in_3, in_2, in_1};
endmodule

module My_ROM (
  input  CE,
  input  A14,
  input  A13,
  input  A12,
  input  A11,
  input  A10,
  input  A9,
  input  A8,
  input  A7,
  input  A6,
  input  A5,
  input  A4,
  input  A3,
  input  A2,
  input  A1,
  input  A0,
  input  OE,
  output [7:0] data
);

  wire and_1_out, not_1_out, not_2_out;
  wire [7:0] rom_1_data;
  wire [14:0] address_1_out_16;

  not not_1 (not_1_out, CE);
  not not_2 (not_2_out, OE);
  address address_1 (
    .in_1(A0), .in_2(A1), .in_3(A2), .in_4(A3), .in_5(A4), .in_6(A5), .in_7(A6), .in_8(A7), .in_9(A8),
    .in_10(A9), .in_11(A10), .in_12(A11), .in_13(A12), .in_14(A13), .in_15(A14), .out_16(address_1_out_16));
  ROM #(.addrWidth(15)) rom_1 (.addr(address_1_out_16), .data(rom_1_data));
  and and_1 (and_1_out, not_1_out, not_2_out);
  assign data = and_1_out ? rom_1_data : 8'bz;  // Controlled_Buffer controlled_buffer_1
endmodule

module My_RAM (
  input  CE,
  input  WR,
  input  A14,
  input  A13,
  input  A12,
  input  A11,
  input  A10,
  input  A9,
  input  A8,
  input  A7,
  input  A6,
  input  A5,
  input  A4,
  input  A3,
  input  A2,
  input  A1,
  input  A0,
  input  OE,
  output [7:0] data
);

  wire not_1_out, not_2_out, not_3_out;
  wire [14:0] address_1_out_16;

  not not_1 (not_1_out, CE);
  not not_2 (not_2_out, WR);
  not not_3 (not_3_out, OE);
  address address_1 (
    .in_1(A0), .in_2(A1), .in_3(A2), .in_4(A3), .in_5(A4), .in_6(A5), .in_7(A6), .in_8(A7), .in_9(A8),
    .in_10(A9), .in_11(A10), .in_12(A11), .in_13(A12), .in_14(A13), .in_15(A14), .out_16(address_1_out_16));
  RAM #(.addrWidth(15)) ram_1 (
    .addr(address_1_out_16), .we(not_2_out), .oe(not_3_out), .clk(not_1_out), .dout(data));  // open: din
endmodule
