// Logisim project 4.3_modify.circ as structural Verilog: 5 circuits, main circuit main
module main (
  input  in_1,
  input  [19:0] in_2,
  input  in_3,
  input  [15:0] in_4,
  input  in_5,
  input  in_6,
  output [15:0] out_7
);

  wire cpu_1_a17, cpu_1_a18, cpu_1_a19, cpu_1_out_18, cpu_1_out_19, n74138_1_pin1, n74138_1_pin2,
       n74138_1_pin3, n74138_1_pin4, n74138_1_pin6, n74138_1_pin9, n74138_1_pin10, n74138_1_pin11,
       n74138_1_pin13, n74138_1_pin14, n74138_1_pin15, nor_1_out, nor_2_out, nor_3_out, nor_4_out, not_1_out,
       not_2_out, not_3_out, not_4_out, not_5_out, not_6_out, not_7_out, not_8_out;
  wire [7:0] cpu_1_w, cpu_1_w_2;
  wire [14:0] cpu_1_out_14;
  wire [15:0] m_rom_2_data;

  _74138 #(.ShowInternalStructure("true")) u_74138_1 (
    .pin1(n74138_1_pin1), .pin2(n74138_1_pin2), .pin3(n74138_1_pin3), .pin4(n74138_1_pin4),
    .pin5(n74138_1_pin4), .pin6(n74138_1_pin6), .pin15(n74138_1_pin15), .pin14(n74138_1_pin14),
    .pin13(n74138_1_pin13), .pin11(n74138_1_pin11), .pin10(n74138_1_pin10), .pin9(n74138_1_pin9));  // open: pin7, pin12
  CPU cpu_1 (
    .RD(in_5), .WR(in_6), .Data_in(in_4), .IO_M(in_1), .address(in_2), .BHE(in_3), .R(m_rom_2_data),
    .Data_out(out_7), .out_8(n74138_1_pin4), .W({cpu_1_w_2, cpu_1_w}), .BHE_out(n74138_1_pin2),
    .A0(n74138_1_pin1), .A19(cpu_1_a19), .out_18(cpu_1_out_18), .out_19(cpu_1_out_19), .A16(n74138_1_pin3),
    .A18(cpu_1_a18), .out_14(cpu_1_out_14), .A17(cpu_1_a17));
  and and_1 (n74138_1_pin6, cpu_1_a17, cpu_1_a18, cpu_1_a19);
  not not_1 (not_1_out, n74138_1_pin11);
  nor nor_1 (nor_1_out, not_1_out, not_2_out);
  not not_2 (not_2_out, n74138_1_pin10);
  m_ROM m_rom_1 (.OE(cpu_1_out_18), .CE(nor_1_out), .address(cpu_1_out_14), .data(m_rom_2_data[15:8]));
  not not_3 (not_3_out, n74138_1_pin9);
  not not_4 (not_4_out, n74138_1_pin11);
  nor nor_2 (nor_2_out, not_4_out, not_3_out);
  m_ROM m_rom_2 (.OE(cpu_1_out_18), .CE(nor_2_out), .address(cpu_1_out_14), .data(m_rom_2_data[7:0]));
  not not_5 (not_5_out, n74138_1_pin15);
  not not_6 (not_6_out, n74138_1_pin14);
  nor nor_3 (nor_3_out, not_5_out, not_6_out);
  m_RAM m_ram_1 (
    .data_in(cpu_1_w_2), .OE(cpu_1_out_18), .CE(nor_3_out), .WR(cpu_1_out_19), .address(cpu_1_out_14),
    .data(m_rom_2_data[15:8]));
  not not_7 (not_7_out, n74138_1_pin15);
  nor nor_4 (nor_4_out, not_7_out, not_8_out);
  not not_8 (not_8_out, n74138_1_pin13);
  m_RAM m_ram_2 (
    .data_in(cpu_1_w), .OE(cpu_1_out_18), .CE(nor_4_out), .WR(cpu_1_out_19), .address(cpu_1_out_14),
    .data(m_rom_2_data[7:0]));
endmodule

module m_ROM (
  input  CE,
  input  [14:0] address,
  input  OE,
  output [7:0] data
);

  wire and_1_out, not_1_out, not_2_out;
  wire [7:0] rom_1_data;

  not not_1 (not_1_out, CE);
  not not_2 (not_2_out, OE);
  ROM #(.addrWidth(15)) rom_1 (.addr(address), .data(rom_1_data));
  and and_1 (and_1_out, not_1_out, not_2_out);
  assign data = and_1_out ? rom_1_data : 8'bz;  // Controlled_Buffer controlled_buffer_1

  // Notes on the sheet:
  //   contents of rom_1 (hex, n*v repeats v):
  //   11
endmodule

module m_RAM (
  input  CE,
  input  WR,
  input  [14:0] address,
  input  OE,
  input  [7:0] data_in,
  output [7:0] data
);

  wire clock_1_out, not_1_out, not_2_out, not_3_out;
  wire [7:0] ram_1_dout;

  not not_1 (not_1_out, CE);
  not not_2 (not_2_out, WR);
  not not_3 (not_3_out, OE);
  Clock clock_1 (.out(clock_1_out));
  RAM #(.addrWidth(15), .readbehav("war"), .trigger("falling")) ram_1 (
    .addr(address), .we(not_2_out), .oe(not_3_out), .clk(clock_1_out), .din(data_in), .dout(ram_1_dout));
  assign data = not_1_out ? ram_1_dout : 8'bz;  // Controlled_Buffer controlled_buffer_1
endmodule

module CPU (
  input  IO_M,
  input  [19:0] address,
  input  BHE,
  input  [15:0] R,
  input  [15:0] Data_in,
  input  RD,
  input  WR,
  output out_8,
  output A0,
  output A16,
  output A17,
  output A18,
  output A19,
  output [14:0] out_14,
  output BHE_out,
  output [15:0] Data_out,
  output [15:0] W,
  output out_18,
  output out_19
);

  wire and_1_out, and_2_out, not_1_out, not_2_out;

  assign W = and_1_out ? Data_in : 16'bz;  // Controlled_Buffer controlled_buffer_1
  not not_1 (not_1_out, RD);
  and and_1 (and_1_out, RD, not_2_out);
  not not_2 (not_2_out, WR);
  divide divide_1 (.in_1(address), .out_2(A0), .out_3(A16), .out_4(A17), .out_5(A18), .out_6(A19), .out_7(out_14));
  and and_2 (and_2_out, WR, not_1_out);
  assign Data_out = and_2_out ? R : 16'bz;  // Controlled_Buffer controlled_buffer_2

  assign BHE_out = BHE;
  assign out_8 = IO_M;
  assign out_18 = RD;
  assign out_19 = WR;
endmodule

module divide (
  input  [19:0] in_1,
  output out_2,
  output out_3,
  output out_4,
  output out_5,
  output out_6,
  output [14:0] out_7
);


  assign out_2 = in_1[0];
  assign out_3 = in_1[16];
  assign out_4 = in_1[17];
  assign out_5 = in_1[18];
  assign out_6 = in_1[19];
  assign out_7 = in_1[15:1];
endmodule
