// Logisim project Multiplie.circ as structural Verilog: 4 circuits, main circuit main
module main (
  input  [4:0] in_1,
  input  [4:0] in_2,
  output [8:0] out_3
);

  wire button_1_out;

  Button button_1 (.out(button_1_out));
  Multipile multipile_1 (.start(button_1_out), .multiplier(in_1), .multiplicand(in_2), .out_4(out_3));
endmodule

module point (
  input  start,
  input  clock,
  output m_out
);

  wire d_ff_1_q, not_1_out;

  D_Flip_Flop d_ff_1 (.D(not_1_out), .clk(start), .Q(d_ff_1_q));  // open: Qn, preset, reset
  not not_1 (not_1_out, start);
  Counter #(.max('h5), .ongoal("stay"), .trigger("falling"), .width(3)) counter_1 (
    .clr(start), .up(d_ff_1_q), .clk(clock), .carry(m_out));  // open: load, count, D, Q
endmodule

module control (
  input  [3:0] multiplicand,
  input  m_select,
  output [4:0] m_out
);

  Multiplexer #(.width(5)) multiplexer_1 (.in0({5{1'b0}}), .in1({1'b0, multiplicand}), .out(m_out), .sel(m_select));
endmodule

module Multipile (
  input  start,
  input  [4:0] multiplier,
  input  [4:0] multiplicand,
  output [8:0] out_4
);

  wire buffer_1_out, clock_1_out, clock_2_out, clock_3_out, not_1_out, point_1_m_out;
  wire [4:0] adder_1_out, control_1_m_out;
  wire [4:4] register_1_q;

  Clock clock_1 (.out(clock_1_out));
  buf buffer_1 (buffer_1_out, not_1_out);
  Clock clock_2 (.out(clock_2_out));
  // Shift_Register #(.length(4), .trigger("falling")) shift_register_1: pin names not known; wires that end beside it: start, buffer_1_out, clock_2_out, out_4[4], multiplier[3], multiplier[2], multiplier[1], multiplier[0], out_4[3], out_4[2], out_4[1]
  point point_1 (.start(start), .clock(clock_1_out), .m_out(point_1_m_out));
  not not_1 (not_1_out, point_1_m_out);
  xor xor_1 (out_4[8], multiplier[4], multiplicand[4]);
  control control_1 (.multiplicand(multiplicand[3:0]), .m_select(out_4[0]), .m_out(control_1_m_out));
  Adder #(.width(5)) adder_1 (
    .a({1'b0, register_1_q[4], out_4[7:5]}), .b(control_1_m_out), .out(adder_1_out));  // open: cin, cout
  Register #(.trigger("falling"), .width(5)) register_1 (
    .D(adder_1_out), .en(not_1_out), .clk(clock_3_out), .Q({register_1_q[4], out_4[7:4]}), .clr(start));
  Clock clock_3 (.out(clock_3_out));
endmodule
