// Logisim project m_CPU.circ as structural Verilog: 8 circuits, main circuit CPU
module CPU (
);

  wire alu_1_zero, and_1_out, control_1_alusrc, control_1_branch, control_1_memetoreg, control_1_memread,
       control_1_memwrite, control_1_regdst, control_1_regwrite;
  wire [4:0] im_1_instruction, im_1_instruction_2, im_1_instruction_5, multiplexer_1_out;
  wire [5:0] alucontrol_1_out_3, control_1_aluop, im_1_instruction_3;
  wire [10:0] im_1_instruction_4;
  wire [31:0] adder_1_out, adder_2_out, alu_1_alu_result, dm_1_read_data, multiplexer_2_out,
       multiplexer_3_out, multiplexer_4_out, pc_1_address, regs_1_read_data1, regs_1_read_data2;

  PC pc_1 (.in_1(multiplexer_3_out), .address(pc_1_address));
  Adder #(.width(32)) adder_1 (.a(pc_1_address), .b(32'h4), .out(adder_1_out));  // open: cin, cout
  IM im_1 (
    .Read_address(pc_1_address),
    .instruction({im_1_instruction_3, im_1_instruction_2, im_1_instruction, im_1_instruction_5, im_1_instruction_4}));
  Multiplexer #(.width(5)) multiplexer_1 (
    .in0(im_1_instruction), .in1(im_1_instruction_5), .out(multiplexer_1_out), .sel(control_1_regdst));
  Control control_1 (
    .in_1(im_1_instruction_3), .RegDst(control_1_regdst), .Branch(control_1_branch),
    .MemRead(control_1_memread), .MemetoReg(control_1_memetoreg), .ALUOP(control_1_aluop),
    .MemWrite(control_1_memwrite), .ALUSrc(control_1_alusrc), .RegWrite(control_1_regwrite));
  Regs regs_1 (
    .RegWrite(control_1_regwrite), .rs(im_1_instruction_2), .rt(im_1_instruction),
    .WriteReg(multiplexer_1_out), .WriteData(multiplexer_4_out), .Read_data1(regs_1_read_data1),
    .Read_data2(regs_1_read_data2));
  Multiplexer #(.width(32)) multiplexer_2 (
    .in0(regs_1_read_data2), .in1({{16{1'b0}}, im_1_instruction_5, im_1_instruction_4}),
    .out(multiplexer_2_out), .sel(control_1_alusrc));
  Adder #(.width(32)) adder_2 (
    .a(adder_1_out), .b({{18{1'b0}}, im_1_instruction_5, im_1_instruction_4[10:2]}), .out(adder_2_out));  // open: cin, cout
  ALUcontrol alucontrol_1 (.instruction(im_1_instruction_4[5:0]), .ALUop(control_1_aluop), .out_3(alucontrol_1_out_3));
  and and_1 (and_1_out, control_1_branch, alu_1_zero);
  Multiplexer #(.width(32)) multiplexer_3 (
    .in0(adder_1_out), .in1(adder_2_out), .out(multiplexer_3_out), .sel(and_1_out));
  ALU alu_1 (
    .op1(regs_1_read_data1), .op2(multiplexer_2_out), .operate(alucontrol_1_out_3), .Zero(alu_1_zero),
    .ALU_result(alu_1_alu_result));
  DM dm_1 (
    .MemWrite(control_1_memwrite), .MemRead(control_1_memread), .Address(alu_1_alu_result),
    .WriteData(regs_1_read_data2), .Read_data(dm_1_read_data));
  Multiplexer #(.width(32)) multiplexer_4 (
    .in0(alu_1_alu_result), .in1(dm_1_read_data), .out(multiplexer_4_out), .sel(control_1_memetoreg));

  // Notes on the sheet:
  //   jeg_address
  //   4
  //   Add
  //   instruction[31-26]
  //   Instruction[25-21]
  //   Instruction[20-16]
  //   Instruction[15-11]
  //   Instruction[15-0]
  //   Instruction[5-0]
  //   Sign-extend
  //   Shift_left 2
endmodule

module PC (
  input  [31:0] in_1,
  output [31:0] address
);

  Register #(.width(32)) register_1 (.D(in_1), .Q(address));  // open: en, clk, clr
endmodule

module IM (
  input  [31:0] Read_address,
  output [31:0] instruction
);
endmodule

module Control (
  input  [5:0] in_1,
  output RegDst,
  output Branch,
  output MemRead,
  output MemetoReg,
  output [5:0] ALUOP,
  output MemWrite,
  output ALUSrc,
  output RegWrite
);
endmodule

module Regs (
  input  RegWrite,
  input  [4:0] rs,
  input  [4:0] rt,
  input  [4:0] WriteReg,
  input  [31:0] WriteData,
  output [31:0] Read_data1,
  output [31:0] Read_data2
);
endmodule

module ALU (
  input  [31:0] op1,
  input  [31:0] op2,
  input  [5:0] operate,
  output Zero,
  output [31:0] ALU_result
);
endmodule

module ALUcontrol (
  input  [5:0] instruction,
  input  [5:0] ALUop,
  output [5:0] out_3
);
endmodule

module DM (
  input  [31:0] Address,
  input  [31:0] WriteData,
  input  MemWrite,
  input  MemRead,
  output [31:0] Read_data
);
endmodule
